// Logisim project 16b_processor_bps16_wds9.circ as structural Verilog: 19 circuits, main circuit main
module main (
  output [1:0] Instruction_Format
);

  wire button_1_out, clock_1_out, comparez_1_result, instrdecode_1_bnez, instrdecode_1_input,
       instrdecode_1_jal, instrdecode_1_ld, instrdecode_1_ldi, instrdecode_1_lpc, instrdecode_1_output,
       instrdecode_1_ra, instrdecode_1_ret, not_1_out, not_2_out, registerfile_1_p3, Reset_2_out, Reset_out;
  wire [2:0] instrdecode_1_rd, instrdecode_1_rs, instrdecode_1_shamt, multiplexer_7_out, registerfile_1_p5,
       registerfile_1_p6;
  wire [3:0] instrdecode_1_opcode;
  wire [5:0] instrdecode_1_immediate;
  wire [6:0] keyboard_1_data;
  wire [15:0] alu_1_result, controlled_buffer_1_out, immsignextender_1_immediateout,
       inputbitextender_1_immediateout, instrdecode_1_address, multiplexer_1_out, multiplexer_2_out,
       multiplexer_3_out, multiplexer_4_out, multiplexer_5_out, multiplexer_6_out, multiplexer_9_out,
       n16b_radder_1_sum, n16b_radder_2_sum, PC_q, registerfile_1_p7, registerfile_1_p8, rom_1_data;

  Multiplexer #(.width(16), .enable("false")) multiplexer_1 (
    .in0(multiplexer_4_out), .in1(multiplexer_2_out), .out(multiplexer_1_out), .sel(instrdecode_1_bnez));
  Multiplexer #(.width(16), .enable("false")) multiplexer_2 (
    .in0(n16b_radder_2_sum), .in1(n16b_radder_1_sum), .out(multiplexer_2_out), .sel(comparez_1_result));
  Counter #(.width(16), .max('hffff)) PC (
    .load(instrdecode_1_lpc), .D(multiplexer_1_out), .count(not_1_out), .Q(PC_q), .clk(clock_1_out),
    .clr(Reset_out));  // open: carry
  not not_1 (not_1_out, instrdecode_1_lpc);
  Button Reset (.out(Reset_out));
  _16b_rAdder u_16b_radder_1 (
    .in1(immsignextender_1_immediateout), .in2(n16b_radder_2_sum), .sum(n16b_radder_1_sum));  // open: cOut
  compareZ comparez_1 (.Immediate(registerfile_1_p7), .result(comparez_1_result));
  _16b_rAdder u_16b_radder_2 (.in1(16'h1), .in2(PC_q), .sum(n16b_radder_2_sum));  // open: cOut
  Clock clock_1 (.out(clock_1_out));
  Multiplexer #(.width(16), .enable("false")) multiplexer_3 (
    .in0(multiplexer_9_out), .in1(n16b_radder_2_sum), .out(multiplexer_3_out), .sel(instrdecode_1_jal));
  Keyboard keyboard_1 (.clk(clock_1_out), .re(instrdecode_1_input), .data(keyboard_1_data));  // open: clr, avail
  Multiplexer #(.width(16), .enable("false")) multiplexer_4 (
    .in0(instrdecode_1_address), .in1(registerfile_1_p7), .out(multiplexer_4_out), .sel(instrdecode_1_ret));
  Multiplexer #(.width(16), .enable("false")) multiplexer_5 (
    .in0(multiplexer_3_out), .in1(immsignextender_1_immediateout), .out(multiplexer_5_out),
    .sel(instrdecode_1_ldi));
  inputBitExtender inputbitextender_1 (.ImmediateIn(keyboard_1_data), .immediateOut(inputbitextender_1_immediateout));
  immSignExtender immsignextender_1 (
    .ImmediateIn(instrdecode_1_immediate), .immediateOut(immsignextender_1_immediateout));
  Multiplexer #(.width(16), .enable("false")) multiplexer_6 (
    .in0(multiplexer_5_out), .in1(inputbitextender_1_immediateout), .out(multiplexer_6_out),
    .sel(instrdecode_1_input));
  ROM #(.addrWidth(16), .dataWidth(16)) rom_1 (.addr(PC_q), .data(rom_1_data));  // open: sel
  Multiplexer #(.width(3), .enable("false")) multiplexer_7 (
    .in0(instrdecode_1_rd), .in1(3'b111), .out(multiplexer_7_out), .sel(instrdecode_1_jal));
  // RegisterFile registerfile_1: pin names not known; wires that end beside it: multiplexer_6_out, clock_1_out, registerfile_1_p3, multiplexer_7_out, registerfile_1_p5, registerfile_1_p6, registerfile_1_p7, registerfile_1_p8
  Multiplexer #(.width(3), .enable("false")) multiplexer_8 (
    .in0(instrdecode_1_rs), .in1(3'b111), .out(registerfile_1_p5), .sel(instrdecode_1_ret));
  instrDecode instrdecode_1 (
    .jal(instrdecode_1_jal), .Instruction(rom_1_data), .LPC(instrdecode_1_lpc), .bnez(instrdecode_1_bnez),
    .ldi(instrdecode_1_ldi), .\input (instrdecode_1_input), .rD(instrdecode_1_rd), .rS(instrdecode_1_rs),
    .rT(registerfile_1_p6), .RA(instrdecode_1_ra), .ret(instrdecode_1_ret), .WE(registerfile_1_p3),
    .shAmt(instrdecode_1_shamt), .opCode(instrdecode_1_opcode), .\output (instrdecode_1_output),
    .Immediate(instrdecode_1_immediate), .Address(instrdecode_1_address), .iFormat(Instruction_Format),
    .ld(instrdecode_1_ld));
  alu alu_1 (
    .rS(registerfile_1_p7), .rT(registerfile_1_p8), .shAmt(instrdecode_1_shamt),
    .opCode(instrdecode_1_opcode), .ImmIn(instrdecode_1_immediate), .Result(alu_1_result));
  Multiplexer #(.width(16), .enable("false")) multiplexer_9 (
    .in0(alu_1_result), .in1(controlled_buffer_1_out), .out(multiplexer_9_out), .sel(instrdecode_1_ra));
  TTY tty_1 (.data(registerfile_1_p7[6:0]), .clk(clock_1_out), .we(instrdecode_1_output), .clr(button_1_out));
  Button button_1 (.out(button_1_out));
  assign controlled_buffer_1_out = not_2_out ? registerfile_1_p8 : 16'bz;  // Controlled_Buffer controlled_buffer_1
  not not_2 (not_2_out, instrdecode_1_ld);
  RAM #(.addrWidth(16), .dataWidth(16)) ram_1 (
    .addr(alu_1_result), .data(controlled_buffer_1_out), .clk(clock_1_out), .ld(instrdecode_1_ld),
    .clr(Reset_2_out));  // open: sel
  Button Reset_2 (.out(Reset_2_out));

  // Notes on the sheet:
  //   contents of rom_1 (hex, n*v repeats v):
  //   204c 9441 84c1 6621 7829 4950 5758 a602 e0c0 b007 d00d 3960 f800 1720 c000 9a80 2048 620d 20c0 52c8
  //   620d 20c6 52c8 6209 20c1 52c8 d07a 8a40 2081 1aa8 d039 208d f400 ac3f 2080 2101 7821 e040 781f 42d8
  //   a63c f200 20d8 6619 32c8 4318 a609 20c9 3658 4718 a605 641b 1490 14d0 1450 b025 c000 2100 20fe 1ae8
  //   20cf 9ac0 2081 7411 4450 58a0 5288 6821 6209 8ac0 a601 b05f 2081 3698 9ac0 20c4 9ac1 8ac1 a601 b03e
  //   2081 3698 9ac1 6824 208f 4510 20c5 34d0 20c1 7619 4698 a602 20c3 18e0 b04d 20c4 9ac1 2040 8ac1 a607
  //   a203 2058 6209 f200 2082 1aa8 c000 2081 3698 9ac1 6824 208f 4510 a202 a401 b062 20d8 6619 14d0 f400
  //   2041 b062 8280 a401 c000 f400 2081 1288 b07a
endmodule

module _16b_rAdder (
  input  [15:0] in1,
  input  [15:0] in2,
  output cOut,
  output [15:0] sum
);

  wire n1b_adder_1_cout, n1b_adder_2_cout, n1b_adder_3_cout, n1b_adder_4_cout, n1b_adder_5_cout,
       n1b_adder_6_cout, n1b_adder_7_cout, n1b_adder_8_cout, n1b_adder_9_cout, n1b_adder_10_cout,
       n1b_adder_11_cout, n1b_adder_12_cout, n1b_adder_13_cout, n1b_adder_14_cout, n1b_adder_15_cout;

  _1b_adder u_1b_adder_1 (.Input_1(in2[0]), .Input_2(in1[0]), .c_in(1'b0), .Sum(sum[0]), .Cout(n1b_adder_1_cout));
  _1b_adder u_1b_adder_2 (
    .Input_1(in2[1]), .Input_2(in1[1]), .c_in(n1b_adder_1_cout), .Sum(sum[1]), .Cout(n1b_adder_2_cout));
  _1b_adder u_1b_adder_3 (
    .Input_1(in2[2]), .Input_2(in1[2]), .c_in(n1b_adder_2_cout), .Sum(sum[2]), .Cout(n1b_adder_3_cout));
  _1b_adder u_1b_adder_4 (
    .Input_1(in2[3]), .Input_2(in1[3]), .c_in(n1b_adder_3_cout), .Sum(sum[3]), .Cout(n1b_adder_4_cout));
  _1b_adder u_1b_adder_5 (
    .Input_1(in2[4]), .Input_2(in1[4]), .c_in(n1b_adder_4_cout), .Sum(sum[4]), .Cout(n1b_adder_5_cout));
  _1b_adder u_1b_adder_6 (
    .Input_1(in2[5]), .Input_2(in1[5]), .c_in(n1b_adder_5_cout), .Sum(sum[5]), .Cout(n1b_adder_6_cout));
  _1b_adder u_1b_adder_7 (
    .Input_1(in2[6]), .Input_2(in1[6]), .c_in(n1b_adder_6_cout), .Sum(sum[6]), .Cout(n1b_adder_7_cout));
  _1b_adder u_1b_adder_8 (
    .Input_1(in2[7]), .Input_2(in1[7]), .c_in(n1b_adder_7_cout), .Sum(sum[7]), .Cout(n1b_adder_8_cout));
  _1b_adder u_1b_adder_9 (
    .Input_1(in2[8]), .Input_2(in1[8]), .c_in(n1b_adder_8_cout), .Sum(sum[8]), .Cout(n1b_adder_9_cout));
  _1b_adder u_1b_adder_10 (
    .Input_1(in2[9]), .Input_2(in1[9]), .c_in(n1b_adder_9_cout), .Sum(sum[9]), .Cout(n1b_adder_10_cout));
  _1b_adder u_1b_adder_11 (
    .Input_1(in2[10]), .Input_2(in1[10]), .c_in(n1b_adder_10_cout), .Sum(sum[10]), .Cout(n1b_adder_11_cout));
  _1b_adder u_1b_adder_12 (
    .Input_1(in2[11]), .Input_2(in1[11]), .c_in(n1b_adder_11_cout), .Sum(sum[11]), .Cout(n1b_adder_12_cout));
  _1b_adder u_1b_adder_13 (
    .Input_1(in2[12]), .Input_2(in1[12]), .c_in(n1b_adder_12_cout), .Sum(sum[12]), .Cout(n1b_adder_13_cout));
  _1b_adder u_1b_adder_14 (
    .Input_1(in2[13]), .Input_2(in1[13]), .c_in(n1b_adder_13_cout), .Sum(sum[13]), .Cout(n1b_adder_14_cout));
  _1b_adder u_1b_adder_15 (
    .Input_1(in2[14]), .Input_2(in1[14]), .c_in(n1b_adder_14_cout), .Sum(sum[14]), .Cout(n1b_adder_15_cout));
  _1b_adder u_1b_adder_16 (.Input_1(in2[15]), .Input_2(in1[15]), .c_in(n1b_adder_15_cout), .Sum(sum[15]), .Cout(cOut));
endmodule

module _1b_adder (
  input  Input_1,
  input  Input_2,
  input  c_in,
  output Sum,
  output Cout
);

  wire and_1_out, and_2_out, xor_1_out;

  xor xor_1 (xor_1_out, Input_1, Input_2);
  and and_1 (and_1_out, Input_1, Input_2);
  xor xor_2 (Sum, xor_1_out, c_in);
  and and_2 (and_2_out, xor_1_out, c_in);
  or or_1 (Cout, and_1_out, and_2_out);
endmodule

// ALU
module alu (
  input  [15:0] rS,
  input  [15:0] rT,
  input  [2:0] shAmt,
  input  [3:0] opCode,
  input  [5:0] ImmIn,
  output [15:0] Result
);

  wire [9:0] multiplexer_1_out;
  wire [15:0] _16bAdder_sum, and_1_out, multiplexer_2_out, multiplexer_3_out, multiplexer_4_out,
       multiplexer_5_out, n16b_radder_1_sum, n16b_radder_2_sum, not_1_out, Rotator_out, xor_1_out;

  assign not_1_out = ~rT;  // NOT_Gate not_1, 16 bits wide
  Multiplexer #(.width(10), .enable("false")) multiplexer_1 (
    .in0({10{1'b0}}), .in1({10{1'b1}}), .out(multiplexer_1_out), .sel(ImmIn[5]));
  _16b_rAdder u_16b_radder_1 (.in1(not_1_out), .in2(16'h1), .sum(n16b_radder_1_sum));  // open: cOut
  _16b_rAdder u_16b_radder_2 (.in1(rS), .in2({multiplexer_1_out, ImmIn}), .sum(n16b_radder_2_sum));  // open: cOut
  Multiplexer #(.width(16), .enable("false")) multiplexer_2 (
    .in0(rT), .in1(n16b_radder_1_sum), .out(multiplexer_2_out), .sel(opCode[1]));
  assign and_1_out = rS & rT;  // AND_Gate and_1, 16 bits wide
  assign xor_1_out = rS ^ rT;  // XOR_Gate xor_1, 16 bits wide
  Rotator Rotator (.ShAmt(shAmt), .In(rS), .L_R(opCode[0]), .Out(Rotator_out));
  Multiplexer #(.width(16), .enable("false")) multiplexer_3 (
    .in0(and_1_out), .in1(xor_1_out), .out(multiplexer_3_out), .sel(opCode[0]));
  _16b_rAdder _16bAdder (.in1(rS), .in2(multiplexer_2_out), .sum(_16bAdder_sum));  // open: cOut
  Multiplexer #(.width(16), .enable("false")) multiplexer_4 (
    .in0(multiplexer_3_out), .in1(Rotator_out), .out(multiplexer_4_out), .sel(opCode[1]));
  Multiplexer #(.width(16), .enable("false")) multiplexer_5 (
    .in0(_16bAdder_sum), .in1(multiplexer_4_out), .out(multiplexer_5_out), .sel(opCode[2]));
  Multiplexer #(.width(16), .enable("false")) multiplexer_6 (
    .in0(multiplexer_5_out), .in1(n16b_radder_2_sum), .out(Result), .sel(opCode[3]));
endmodule

module instrDecode (
  input  [15:0] Instruction,
  output ldi,
  output \input ,
  output [2:0] rD,
  output [2:0] rS,
  output [2:0] rT,
  output [2:0] shAmt,
  output jal,
  output \output ,
  output [3:0] opCode,
  output LPC,
  output [5:0] Immediate,
  output [15:0] Address,
  output RA,
  output ret,
  output WE,
  output [1:0] iFormat,
  output bnez,
  output ld
);

  wire and_1_out, not_1_out, or_1_out, or_2_out, xor_1_out;

  or or_1 (or_1_out, and_1_out, \input , ldi);
  ldi ldi_1 (.opCode(Instruction[15:12]), .ldi(ldi));
  and and_1 (and_1_out, ld, RA);
  RAMAccess ramaccess_1 (.OpCode(Instruction[15:12]), .ld(ld), .RAMAccess(RA));
  \input  input_1 (.opCode(Instruction[15:12]), .\input (\input ));
  jal jal_1 (.opCode(Instruction[15:12]), .jal(jal));
  loadPC loadpc_1 (.opCode(Instruction[15:12]), .LPC(LPC));
  ret ret_1 (.opCode(Instruction[15:12]), .ret(ret));
  wEnable wenable_1 (.opCode(Instruction[15:12]), .WE(WE));
  bnez bnez_1 (.opCode(Instruction[15:12]), .bnez(bnez));
  xor xor_1 (xor_1_out, Instruction[13], Instruction[14]);
  Multiplexer #(.width(3), .enable("false")) multiplexer_1 (
    .in0(Instruction[5:3]), .in1(Instruction[8:6]), .out(rD), .sel(or_1_out));
  or or_2 (or_2_out, Instruction[12], Instruction[14]);
  not not_1 (not_1_out, Instruction[15]);
  and and_2 (iFormat[0], or_2_out, not_1_out);
  and and_3 (iFormat[1], Instruction[12], Instruction[15], xor_1_out);
  \output  output_1 (.opCode(Instruction[15:12]), .\output (\output ));

  assign Address = {4'b0000, Instruction[11:0]};
  assign Immediate = Instruction[5:0];
  assign opCode = Instruction[15:12];
  assign rS = Instruction[11:9];
  assign rT = Instruction[8:6];
  assign shAmt = Instruction[2:0];
endmodule

module wEnable (
  input  [3:0] opCode,
  output WE
);

  wire and_1_out, and_2_out, and_3_out, not_1_out, not_2_out, not_3_out, not_4_out;

  not not_1 (not_1_out, opCode[0]);
  not not_2 (not_2_out, opCode[1]);
  not not_3 (not_3_out, opCode[2]);
  not not_4 (not_4_out, opCode[3]);
  and and_1 (and_1_out, not_1_out, opCode[3], not_3_out);
  and and_2 (and_2_out, opCode[3], opCode[1], not_1_out);
  and and_3 (and_3_out, opCode[0], not_2_out, opCode[2], opCode[3]);
  or or_1 (WE, and_3_out, and_2_out, and_1_out, not_4_out);
endmodule

module ret (
  input  [3:0] opCode,
  output ret
);

  wire not_1_out, not_2_out;

  not not_1 (not_1_out, opCode[0]);
  not not_2 (not_2_out, opCode[1]);
  and and_1 (ret, not_1_out, not_2_out, opCode[2], opCode[3]);
endmodule

module RAMAccess (
  input  [3:0] OpCode,
  output ld,
  output RAMAccess
);

  wire not_2_out, not_3_out;

  not not_1 (ld, OpCode[0]);
  not not_2 (not_2_out, OpCode[1]);
  and and_1 (RAMAccess, not_2_out, not_3_out, OpCode[3]);
  not not_3 (not_3_out, OpCode[2]);
endmodule

module loadPC (
  input  [3:0] opCode,
  output LPC
);

  wire xor_1_out;

  xor xor_1 (xor_1_out, opCode[1], opCode[2]);
  and and_1 (LPC, xor_1_out, opCode[3]);
endmodule

module jal (
  input  [3:0] opCode,
  output jal
);

  wire not_1_out;

  not not_1 (not_1_out, opCode[1]);
  and and_1 (jal, opCode[0], not_1_out, opCode[2], opCode[3]);
endmodule

module immSignExtender (
  input  [5:0] ImmediateIn,
  output [15:0] immediateOut
);

  Multiplexer #(.width(10), .enable("false")) multiplexer_1 (
    .in0({10{1'b0}}), .in1({10{1'b1}}), .out(immediateOut[15:6]), .sel(ImmediateIn[5]));

  assign immediateOut[5:0] = ImmediateIn;
endmodule

module compareZ (
  input  [15:0] Immediate,
  output result
);

  wire and_1_out, not_1_out, not_2_out, not_3_out, not_4_out, not_5_out, not_6_out, not_7_out, not_8_out,
       not_9_out, not_10_out, not_11_out, not_12_out, not_13_out, not_14_out, not_15_out, not_16_out;

  not not_1 (not_1_out, Immediate[0]);
  not not_2 (not_2_out, Immediate[1]);
  not not_3 (not_3_out, Immediate[2]);
  not not_4 (not_4_out, Immediate[3]);
  not not_5 (not_5_out, Immediate[4]);
  not not_6 (not_6_out, Immediate[5]);
  not not_7 (not_7_out, Immediate[6]);
  not not_8 (not_8_out, Immediate[7]);
  and and_1 (and_1_out, not_1_out, not_2_out, not_3_out, not_4_out, not_5_out, not_6_out, not_7_out, not_8_out, not_9_out, not_10_out, not_11_out, not_12_out, not_13_out, not_14_out, not_15_out, not_16_out);
  not not_9 (not_9_out, Immediate[9]);
  not not_10 (not_10_out, Immediate[10]);
  not not_11 (not_11_out, Immediate[11]);
  not not_12 (not_12_out, Immediate[12]);
  not not_13 (not_13_out, Immediate[13]);
  not not_14 (not_14_out, Immediate[14]);
  not not_15 (not_15_out, Immediate[15]);
  not not_16 (not_16_out, Immediate[8]);
  not not_17 (result, and_1_out);
endmodule

module bnez (
  input  [3:0] opCode,
  output bnez
);

  wire not_1_out, not_2_out;

  not not_1 (not_1_out, opCode[0]);
  not not_2 (not_2_out, opCode[2]);
  and and_1 (bnez, not_1_out, opCode[1], not_2_out, opCode[3]);
endmodule

module _1b_rotate (
  input  [15:0] In,
  input  L_R,
  output [15:0] Out
);

  Multiplexer #(.width(16), .enable("false")) multiplexer_1 (
    .in0({In[14:0], In[15]}), .in1({In[0], In[15:1]}), .out(Out), .sel(L_R));
endmodule

module Rotator (
  input  [2:0] ShAmt,
  input  [15:0] In,
  input  L_R,
  output [15:0] Out
);

  wire [15:0] multiplexer_1_out, multiplexer_2_out, n1b_rotate_1_out, n1b_rotate_2_out, n1b_rotate_3_out,
       n1b_rotate_4_out, n1b_rotate_5_out, n1b_rotate_6_out, n1b_rotate_7_out;

  _1b_rotate u_1b_rotate_1 (.In(In), .L_R(L_R), .Out(n1b_rotate_1_out));
  _1b_rotate u_1b_rotate_2 (.In(n1b_rotate_1_out), .L_R(L_R), .Out(n1b_rotate_2_out));
  _1b_rotate u_1b_rotate_3 (.In(n1b_rotate_2_out), .L_R(L_R), .Out(n1b_rotate_3_out));
  _1b_rotate u_1b_rotate_4 (.In(n1b_rotate_3_out), .L_R(L_R), .Out(n1b_rotate_4_out));
  Multiplexer #(.width(16), .enable("false")) multiplexer_1 (
    .in0(In), .in1(n1b_rotate_4_out), .out(multiplexer_1_out), .sel(ShAmt[2]));
  _1b_rotate u_1b_rotate_5 (.In(n1b_rotate_6_out), .L_R(L_R), .Out(n1b_rotate_5_out));
  _1b_rotate u_1b_rotate_6 (.In(multiplexer_1_out), .L_R(L_R), .Out(n1b_rotate_6_out));
  Multiplexer #(.width(16), .enable("false")) multiplexer_2 (
    .in0(multiplexer_1_out), .in1(n1b_rotate_5_out), .out(multiplexer_2_out), .sel(ShAmt[1]));
  Multiplexer #(.width(16), .enable("false")) multiplexer_3 (
    .in0(multiplexer_2_out), .in1(n1b_rotate_7_out), .out(Out), .sel(ShAmt[0]));
  _1b_rotate u_1b_rotate_7 (.In(multiplexer_2_out), .L_R(L_R), .Out(n1b_rotate_7_out));
endmodule

module ldi (
  input  [3:0] opCode,
  output ldi
);

  wire not_1_out, not_2_out, not_3_out;

  not not_1 (not_1_out, opCode[0]);
  not not_2 (not_2_out, opCode[2]);
  not not_3 (not_3_out, opCode[3]);
  and and_1 (ldi, not_1_out, opCode[1], not_2_out, not_3_out);
endmodule

module \input  (
  input  [3:0] opCode,
  output \input 
);

  wire not_1_out;

  not not_1 (not_1_out, opCode[0]);
  and and_1 (\input , not_1_out, opCode[1], opCode[2], opCode[3]);
endmodule

module inputBitExtender (
  input  [6:0] ImmediateIn,
  output [15:0] immediateOut
);


  assign immediateOut = {{9{1'b0}}, ImmediateIn};
endmodule

module \output  (
  input  [3:0] opCode,
  output \output 
);

  and and_1 (\output , opCode[0], opCode[1], opCode[2], opCode[3]);
endmodule
